// Logisim project ContadorSincrono.circ as structural Verilog: 1 circuit, main circuit main
module main (
);

  wire clock_1_out;

  Clock clock_1 (.out(clock_1_out));
  J_K_Flip_Flop j_k_ff_1 (.clk(clock_1_out));  // open: J, K, Q, Qn, preset, en, reset
  J_K_Flip_Flop j_k_ff_2 (.clk(clock_1_out));  // open: J, K, Q, Qn, preset, en, reset
  J_K_Flip_Flop j_k_ff_3 (.clk(clock_1_out));  // open: J, K, Q, Qn, preset, en, reset
endmodule
