// Logisim project Processador.circ as structural Verilog: 18 circuits, main circuit main
module main (
  input  _11,
  input  _10,
  input  _9,
  input  _8,
  input  _7,
  input  _6,
  input  _5,
  input  _4,
  input  _3,
  input  _2,
  input  _1,
  input  _0,
  input  clock_manual_para_teste,
  input  reset
);

  wire banco_de_registradores_1_r0, banco_de_registradores_1_r1, banco_de_registradores_1_r2,
       banco_de_registradores_1_r3, banco_de_registradores_1_x0, banco_de_registradores_1_x1,
       banco_de_registradores_1_x2, banco_de_registradores_1_x3, decod_display_7_segmentos_1_a,
       decod_display_7_segmentos_1_b, decod_display_7_segmentos_1_c, decod_display_7_segmentos_1_d,
       decod_display_7_segmentos_1_e, decod_display_7_segmentos_1_f, decod_display_7_segmentos_1_g,
       expansor_3_4bits_1__0_2, expansor_3_4bits_1__1_2, expansor_3_4bits_1__2_2, expansor_3_4bits_1__3,
       multiplexador_8_4_1__0, multiplexador_8_4_1__1, multiplexador_8_4_1__2, multiplexador_8_4_1__3,
       registrador_de_instrucao_1_op0, registrador_de_instrucao_1_op1, registrador_de_instrucao_1_op2,
       registrador_de_instrucao_1_r1_0, registrador_de_instrucao_1_r1_1, registrador_de_instrucao_1_r1_2,
       registrador_de_instrucao_1_wr_0, registrador_de_instrucao_1_wr_1, registrador_de_instrucao_1_wr_2,
       registrador_de_instrucao_1_x_0, registrador_de_instrucao_1_x_1, registrador_de_instrucao_1_x_2,
       ula_1__0, ula_1__1, ula_1__2, ula_1__3, unidade_de_controle_1_aluop_0, unidade_de_controle_1_aluop_1,
       unidade_de_controle_1_alusrc, unidade_de_controle_1_regwrite;

  Registrador_de_instrucao registrador_de_instrucao_1 (
    .clock(clock_manual_para_teste), ._11_pos_bit(_11), ._10_pos_bit(_10), ._9_pos_bit(_9), ._8_pos_bit(_8),
    ._7_pos_bit(_7), ._6_pos_bit(_6), ._5_pos_bit(_5), ._4_pos_bit(_4), ._3_pos_bit(_3), ._2_pos_bit(_2),
    ._1_pos_bit(_1), ._0_pos_bit(_0), .op2(registrador_de_instrucao_1_op2),
    .op1(registrador_de_instrucao_1_op1), .op0(registrador_de_instrucao_1_op0),
    .r1_2(registrador_de_instrucao_1_r1_2), .r1_1(registrador_de_instrucao_1_r1_1),
    .r1_0(registrador_de_instrucao_1_r1_0), .x_2(registrador_de_instrucao_1_x_2),
    .x_1(registrador_de_instrucao_1_x_1), .x_0(registrador_de_instrucao_1_x_0),
    .wr_2(registrador_de_instrucao_1_wr_2), .wr_1(registrador_de_instrucao_1_wr_1),
    .wr_0(registrador_de_instrucao_1_wr_0), .reset(reset));
  Unidade_de_controle unidade_de_controle_1 (
    .op2(registrador_de_instrucao_1_op2), .op1(registrador_de_instrucao_1_op1),
    .op0(registrador_de_instrucao_1_op0), .ALUOp_1(unidade_de_controle_1_aluop_1),
    .ALUOp_0(unidade_de_controle_1_aluop_0), .ALUSrc(unidade_de_controle_1_alusrc),
    .RegWrite(unidade_de_controle_1_regwrite));
  Expansor_3_4bits expansor_3_4bits_1 (
    ._2(registrador_de_instrucao_1_x_2), ._1(registrador_de_instrucao_1_x_1),
    ._0(registrador_de_instrucao_1_x_0), ._3(expansor_3_4bits_1__3), ._2_2(expansor_3_4bits_1__2_2),
    ._1_2(expansor_3_4bits_1__1_2), ._0_2(expansor_3_4bits_1__0_2));
  Banco_de_registradores banco_de_registradores_1 (
    .r1_2(registrador_de_instrucao_1_r1_2), .r1_1(registrador_de_instrucao_1_r1_1),
    .r1_0(registrador_de_instrucao_1_r1_0), .Clock(clock_manual_para_teste),
    .r3(banco_de_registradores_1_r3), .r2(banco_de_registradores_1_r2), .r1(banco_de_registradores_1_r1),
    .r0(banco_de_registradores_1_r0), .x_2(registrador_de_instrucao_1_x_2),
    .x_1(registrador_de_instrucao_1_x_1), .x_0(registrador_de_instrucao_1_x_0),
    .x0(banco_de_registradores_1_x0), .x1(banco_de_registradores_1_x1), .x3(banco_de_registradores_1_x3),
    .x2(banco_de_registradores_1_x2), .wr_2(registrador_de_instrucao_1_wr_2),
    .wr_1(registrador_de_instrucao_1_wr_1), .wr_0(registrador_de_instrucao_1_wr_0), .wd_2(ula_1__2),
    .wd_1(ula_1__1), .wd_0(ula_1__0), .wd_3(ula_1__3), .RegWrite(unidade_de_controle_1_regwrite),
    .Reset(reset));
  Multiplexador_8_4 multiplexador_8_4_1 (
    .control(unidade_de_controle_1_alusrc), .x3(banco_de_registradores_1_x3),
    .x2(banco_de_registradores_1_x2), .x1(banco_de_registradores_1_x1), .x0(banco_de_registradores_1_x0),
    .y3(expansor_3_4bits_1__3), .y2(expansor_3_4bits_1__2_2), .y1(expansor_3_4bits_1__1_2),
    .y0(expansor_3_4bits_1__0_2), ._3(multiplexador_8_4_1__3), ._2(multiplexador_8_4_1__2),
    ._1(multiplexador_8_4_1__1), ._0(multiplexador_8_4_1__0));
  ULA ula_1 (
    .ALUop1(unidade_de_controle_1_aluop_1), .ALUop0(unidade_de_controle_1_aluop_0),
    .x3(banco_de_registradores_1_r3), .x2(banco_de_registradores_1_r2), .x1(banco_de_registradores_1_r1),
    .x0(banco_de_registradores_1_r0), .y3(multiplexador_8_4_1__3), .y2(multiplexador_8_4_1__2),
    .y1(multiplexador_8_4_1__1), .y0(multiplexador_8_4_1__0), ._3(ula_1__3), ._2(ula_1__2), ._1(ula_1__1),
    ._0(ula_1__0));
  Decod_display_7_segmentos decod_display_7_segmentos_1 (
    .a(decod_display_7_segmentos_1_a), .b(decod_display_7_segmentos_1_b), .c(decod_display_7_segmentos_1_c),
    .d(decod_display_7_segmentos_1_d), .e(decod_display_7_segmentos_1_e), .f(decod_display_7_segmentos_1_f),
    .g(decod_display_7_segmentos_1_g), ._3(ula_1__3), ._2(ula_1__2), ._1(ula_1__1), ._0(ula_1__0));
  _7_Segment_Display u_7_segment_display_1 (
    .g(decod_display_7_segmentos_1_g), .f(decod_display_7_segmentos_1_f), .a(decod_display_7_segmentos_1_a),
    .b(decod_display_7_segmentos_1_b), .e(decod_display_7_segmentos_1_e), .d(decod_display_7_segmentos_1_d),
    .c(decod_display_7_segmentos_1_c));  // open: dp

  // Notes on the sheet:
  //   op | r1 | x | wr
  //   r1 = register 1 source
  //   x = register or immediate source
  //   wr = register to write to
  //   wd = write data from the ALU
endmodule

module registrador_4bit (
  input  clock,
  input  _3_pos_bit,
  input  _2_pos_bit,
  input  _1_pos_bit,
  input  _0_pos_bit,
  input  enable,
  input  reset,
  output _3_pos_bit_2,
  output _2_pos_bit_2,
  output _1_pos_bit_2,
  output _0_pos_bit_2
);

  D_Flip_Flop d_ff_1 (.clk(clock), .D(_3_pos_bit), .Q(_3_pos_bit_2), .en(enable), .reset(reset));  // open: Qn, preset
  D_Flip_Flop d_ff_2 (.clk(clock), .D(_2_pos_bit), .Q(_2_pos_bit_2), .en(enable), .reset(reset));  // open: Qn, preset
  D_Flip_Flop d_ff_3 (.clk(clock), .D(_1_pos_bit), .Q(_1_pos_bit_2), .en(enable), .reset(reset));  // open: Qn, preset
  D_Flip_Flop d_ff_4 (.clk(clock), .D(_0_pos_bit), .Q(_0_pos_bit_2), .en(enable), .reset(reset));  // open: Qn, preset
endmodule

module registrador_8bit (
  input  clock,
  input  _7_pos_bit,
  input  _6_pos_bit,
  input  _5_pos_bit,
  input  _4_pos_bit,
  input  _3_pos_bit,
  input  _2_pos_bit,
  input  _1_pos_bit,
  input  _0_pos_bit,
  input  enable,
  input  reset,
  output _7_pos_bit_2,
  output _6_pos_bit_2,
  output _5_pos_bit_2,
  output _4_pos_bit_2,
  output _3_pos_bit_2,
  output _2_pos_bit_2,
  output _1_pos_bit_2,
  output _0_pos_bit_2
);

  registrador_4bit registrador_4bit_1 (
    .clock(clock), ._3_pos_bit(_7_pos_bit), ._2_pos_bit(_6_pos_bit), ._1_pos_bit(_5_pos_bit),
    ._0_pos_bit(_4_pos_bit), ._3_pos_bit_2(_7_pos_bit_2), ._2_pos_bit_2(_6_pos_bit_2),
    ._1_pos_bit_2(_5_pos_bit_2), ._0_pos_bit_2(_4_pos_bit_2), .enable(enable), .reset(reset));
  registrador_4bit registrador_4bit_2 (
    .clock(clock), ._3_pos_bit(_3_pos_bit), ._2_pos_bit(_2_pos_bit), ._1_pos_bit(_1_pos_bit),
    ._0_pos_bit(_0_pos_bit), ._3_pos_bit_2(_3_pos_bit_2), ._2_pos_bit_2(_2_pos_bit_2),
    ._1_pos_bit_2(_1_pos_bit_2), ._0_pos_bit_2(_0_pos_bit_2), .enable(enable), .reset(reset));
endmodule

module ULA (
  input  ALUop1,
  input  ALUop0,
  input  x3,
  input  x2,
  input  x1,
  input  x0,
  input  y3,
  input  y2,
  input  y1,
  input  y0,
  output _3,
  output _2,
  output _1,
  output _0
);

  wire add_sub_4bit_1_s0, add_sub_4bit_1_s1, add_sub_4bit_1_s2, add_sub_4bit_1_s3;

  add_sub_4bit add_sub_4bit_1 (
    .Sub(ALUop0), .a3(x3), .b3(y3), .a2(x2), .b2(y2), .a1(x1), .b1(y1), .a0(x0), .b0(y0),
    .s3(add_sub_4bit_1_s3), .s2(add_sub_4bit_1_s2), .s1(add_sub_4bit_1_s1), .s0(add_sub_4bit_1_s0));  // open: CarryOut
  Multiplexador_8_4 multiplexador_8_4_1 (
    .control(ALUop1), .x3(add_sub_4bit_1_s3), .x2(add_sub_4bit_1_s2), .x1(add_sub_4bit_1_s1),
    .x0(add_sub_4bit_1_s0), .y3(y3), .y2(y2), .y1(y1), .y0(y0), ._3(_3), ._2(_2), ._1(_1), ._0(_0));

  // Notes on the sheet:
  //   00 = add
  //   01 = sub
  //   10 = mov
  //   11 = exULA
endmodule

module Registrador_de_instrucao (
  input  clock,
  input  _11_pos_bit,
  input  _10_pos_bit,
  input  _9_pos_bit,
  input  _8_pos_bit,
  input  _7_pos_bit,
  input  _6_pos_bit,
  input  _5_pos_bit,
  input  _4_pos_bit,
  input  _3_pos_bit,
  input  _2_pos_bit,
  input  _1_pos_bit,
  input  _0_pos_bit,
  input  reset,
  output op2,
  output op1,
  output op0,
  output r1_2,
  output r1_1,
  output r1_0,
  output x_2,
  output x_1,
  output x_0,
  output wr_2,
  output wr_1,
  output wr_0
);

  registrador_4bit registrador_4bit_1 (
    .clock(clock), ._3_pos_bit(_11_pos_bit), ._2_pos_bit(_10_pos_bit), ._1_pos_bit(_9_pos_bit),
    ._0_pos_bit(_8_pos_bit), ._3_pos_bit_2(op2), ._2_pos_bit_2(op1), ._1_pos_bit_2(op0), ._0_pos_bit_2(r1_2),
    .enable(1'b1), .reset(reset));
  registrador_8bit registrador_8bit_1 (
    .clock(clock), ._7_pos_bit(_7_pos_bit), ._6_pos_bit(_6_pos_bit), ._5_pos_bit(_5_pos_bit),
    ._4_pos_bit(_4_pos_bit), ._3_pos_bit(_3_pos_bit), ._2_pos_bit(_2_pos_bit), ._1_pos_bit(_1_pos_bit),
    ._0_pos_bit(_0_pos_bit), ._7_pos_bit_2(r1_1), ._6_pos_bit_2(r1_0), ._5_pos_bit_2(x_2),
    ._4_pos_bit_2(x_1), ._3_pos_bit_2(x_0), ._2_pos_bit_2(wr_2), ._1_pos_bit_2(wr_1), ._0_pos_bit_2(wr_0),
    .enable(1'b1), .reset(reset));
endmodule

module Banco_de_registradores (
  input  r1_2,
  input  r1_1,
  input  r1_0,
  input  Clock,
  input  wd_3,
  input  wd_2,
  input  wd_1,
  input  wd_0,
  input  wr_2,
  input  wr_1,
  input  wr_0,
  input  RegWrite,
  input  Reset,
  input  x_2,
  input  x_1,
  input  x_0,
  output r3,
  output r2,
  output r1,
  output r0,
  output x3,
  output x2,
  output x1,
  output x0
);

  wire demultiplexador_1_8_1__0, demultiplexador_1_8_1__1, demultiplexador_1_8_1__2,
       demultiplexador_1_8_1__3, demultiplexador_1_8_1__4, demultiplexador_1_8_1__5,
       demultiplexador_1_8_1__6, demultiplexador_1_8_1__7, R0__0_pos_bit_2, R0__1_pos_bit_2, R0__2_pos_bit_2,
       R0__3_pos_bit_2, R1__0_pos_bit_2, R1__1_pos_bit_2, R1__2_pos_bit_2, R1__3_pos_bit_2, R2__0_pos_bit_2,
       R2__1_pos_bit_2, R2__2_pos_bit_2, R2__3_pos_bit_2, R3__0_pos_bit_2, R3__1_pos_bit_2, R3__2_pos_bit_2,
       R3__3_pos_bit_2, R4__0_pos_bit_2, R4__1_pos_bit_2, R4__2_pos_bit_2, R4__3_pos_bit_2, R5__0_pos_bit_2,
       R5__1_pos_bit_2, R5__2_pos_bit_2, R5__3_pos_bit_2, R6__0_pos_bit_2, R6__1_pos_bit_2, R6__2_pos_bit_2,
       R6__3_pos_bit_2, R7__0_pos_bit_2, R7__1_pos_bit_2, R7__2_pos_bit_2, R7__3_pos_bit_2;

  Demultiplexador_1_8 demultiplexador_1_8_1 (
    .control0(wr_0), .control1(wr_1), .control2(wr_2), .\input (RegWrite), ._0(demultiplexador_1_8_1__0),
    ._1(demultiplexador_1_8_1__1), ._2(demultiplexador_1_8_1__2), ._3(demultiplexador_1_8_1__3),
    ._4(demultiplexador_1_8_1__4), ._5(demultiplexador_1_8_1__5), ._6(demultiplexador_1_8_1__6),
    ._7(demultiplexador_1_8_1__7));
  registrador_4bit u_R0 (
    .clock(Clock), ._3_pos_bit(wd_3), ._2_pos_bit(wd_2), ._1_pos_bit(wd_1), ._0_pos_bit(wd_0),
    ._3_pos_bit_2(R0__3_pos_bit_2), ._2_pos_bit_2(R0__2_pos_bit_2), ._1_pos_bit_2(R0__1_pos_bit_2),
    ._0_pos_bit_2(R0__0_pos_bit_2), .enable(demultiplexador_1_8_1__0), .reset(Reset));
  registrador_4bit u_R1 (
    .clock(Clock), ._3_pos_bit(wd_3), ._2_pos_bit(wd_2), ._1_pos_bit(wd_1), ._0_pos_bit(wd_0),
    ._3_pos_bit_2(R1__3_pos_bit_2), ._2_pos_bit_2(R1__2_pos_bit_2), ._1_pos_bit_2(R1__1_pos_bit_2),
    ._0_pos_bit_2(R1__0_pos_bit_2), .enable(demultiplexador_1_8_1__1), .reset(Reset));
  registrador_4bit u_R2 (
    .clock(Clock), ._3_pos_bit(wd_3), ._2_pos_bit(wd_2), ._1_pos_bit(wd_1), ._0_pos_bit(wd_0),
    ._3_pos_bit_2(R2__3_pos_bit_2), ._2_pos_bit_2(R2__2_pos_bit_2), ._1_pos_bit_2(R2__1_pos_bit_2),
    ._0_pos_bit_2(R2__0_pos_bit_2), .enable(demultiplexador_1_8_1__2));  // open: reset
  registrador_4bit u_R3 (
    .clock(Clock), ._3_pos_bit(wd_3), ._2_pos_bit(wd_2), ._1_pos_bit(wd_1), ._0_pos_bit(wd_0),
    ._3_pos_bit_2(R3__3_pos_bit_2), ._2_pos_bit_2(R3__2_pos_bit_2), ._1_pos_bit_2(R3__1_pos_bit_2),
    ._0_pos_bit_2(R3__0_pos_bit_2), .enable(demultiplexador_1_8_1__3), .reset(Reset));
  Multiplexador_8_1 _3 (
    .control0(r1_0), .control1(r1_1), .control2(r1_2), .a(R0__3_pos_bit_2), .b(R1__3_pos_bit_2),
    .c(R2__3_pos_bit_2), .d(R3__3_pos_bit_2), .e(R4__3_pos_bit_2), .f(R5__3_pos_bit_2), .g(R6__3_pos_bit_2),
    .h(R7__3_pos_bit_2), .out_12(r3));
  Multiplexador_8_1 _3_2 (
    .control0(x_0), .control1(x_1), .control2(x_2), .a(R0__3_pos_bit_2), .b(R1__3_pos_bit_2),
    .c(R2__3_pos_bit_2), .d(R3__3_pos_bit_2), .e(R4__3_pos_bit_2), .f(R5__3_pos_bit_2), .g(R6__3_pos_bit_2),
    .h(R7__3_pos_bit_2), .out_12(x3));
  Multiplexador_8_1 _2 (
    .control0(r1_0), .control1(r1_1), .control2(r1_2), .a(R0__2_pos_bit_2), .b(R1__2_pos_bit_2),
    .c(R2__2_pos_bit_2), .d(R3__2_pos_bit_2), .e(R4__2_pos_bit_2), .f(R5__2_pos_bit_2), .g(R6__2_pos_bit_2),
    .h(R7__2_pos_bit_2), .out_12(r2));
  Multiplexador_8_1 _2_2 (
    .control0(x_0), .control1(x_1), .control2(x_2), .a(R0__2_pos_bit_2), .b(R1__2_pos_bit_2),
    .c(R2__2_pos_bit_2), .d(R3__2_pos_bit_2), .e(R4__2_pos_bit_2), .f(R5__2_pos_bit_2), .g(R6__2_pos_bit_2),
    .h(R7__2_pos_bit_2), .out_12(x2));
  Multiplexador_8_1 _1 (
    .control0(r1_0), .control1(r1_1), .control2(r1_2), .a(R0__1_pos_bit_2), .b(R1__1_pos_bit_2),
    .c(R2__1_pos_bit_2), .d(R3__1_pos_bit_2), .e(R4__1_pos_bit_2), .f(R5__1_pos_bit_2), .g(R6__1_pos_bit_2),
    .h(R7__1_pos_bit_2), .out_12(r1));
  Multiplexador_8_1 _1_2 (
    .control0(x_0), .control1(x_1), .control2(x_2), .a(R0__1_pos_bit_2), .b(R1__1_pos_bit_2),
    .c(R2__1_pos_bit_2), .d(R3__1_pos_bit_2), .e(R4__1_pos_bit_2), .f(R5__1_pos_bit_2), .g(R6__1_pos_bit_2),
    .h(R7__1_pos_bit_2), .out_12(x1));
  Multiplexador_8_1 _0 (
    .control0(r1_0), .control1(r1_1), .control2(r1_2), .a(R0__0_pos_bit_2), .b(R1__0_pos_bit_2),
    .c(R2__0_pos_bit_2), .d(R3__0_pos_bit_2), .e(R4__0_pos_bit_2), .f(R5__0_pos_bit_2), .g(R6__0_pos_bit_2),
    .h(R7__0_pos_bit_2), .out_12(r0));
  Multiplexador_8_1 _0_2 (
    .control0(x_0), .control1(x_1), .control2(x_2), .a(R0__0_pos_bit_2), .b(R1__0_pos_bit_2),
    .c(R2__0_pos_bit_2), .d(R3__0_pos_bit_2), .e(R4__0_pos_bit_2), .f(R5__0_pos_bit_2), .g(R6__0_pos_bit_2),
    .h(R7__0_pos_bit_2), .out_12(x0));
  registrador_4bit R4 (
    .clock(Clock), ._3_pos_bit(wd_3), ._2_pos_bit(wd_2), ._1_pos_bit(wd_1), ._0_pos_bit(wd_0),
    ._3_pos_bit_2(R4__3_pos_bit_2), ._2_pos_bit_2(R4__2_pos_bit_2), ._1_pos_bit_2(R4__1_pos_bit_2),
    ._0_pos_bit_2(R4__0_pos_bit_2), .enable(demultiplexador_1_8_1__4), .reset(Reset));
  registrador_4bit R5 (
    .clock(Clock), ._3_pos_bit(wd_3), ._2_pos_bit(wd_2), ._1_pos_bit(wd_1), ._0_pos_bit(wd_0),
    ._3_pos_bit_2(R5__3_pos_bit_2), ._2_pos_bit_2(R5__2_pos_bit_2), ._1_pos_bit_2(R5__1_pos_bit_2),
    ._0_pos_bit_2(R5__0_pos_bit_2), .enable(demultiplexador_1_8_1__5), .reset(Reset));
  registrador_4bit R6 (
    .clock(Clock), ._3_pos_bit(wd_3), ._2_pos_bit(wd_2), ._1_pos_bit(wd_1), ._0_pos_bit(wd_0),
    ._3_pos_bit_2(R6__3_pos_bit_2), ._2_pos_bit_2(R6__2_pos_bit_2), ._1_pos_bit_2(R6__1_pos_bit_2),
    ._0_pos_bit_2(R6__0_pos_bit_2), .enable(demultiplexador_1_8_1__6), .reset(Reset));
  registrador_4bit R7 (
    .clock(Clock), ._3_pos_bit(wd_3), ._2_pos_bit(wd_2), ._1_pos_bit(wd_1), ._0_pos_bit(wd_0),
    ._3_pos_bit_2(R7__3_pos_bit_2), ._2_pos_bit_2(R7__2_pos_bit_2), ._1_pos_bit_2(R7__1_pos_bit_2),
    ._0_pos_bit_2(R7__0_pos_bit_2), .enable(demultiplexador_1_8_1__7), .reset(Reset));

  // Notes on the sheet:
  //   rw deve escolhber para onde mandar o clock e passar o wd
  //   r1 = register 1 source
  //   wr = register to write to
  //   x = register or immediate source
  //   wd = write data from the ALU
endmodule

module Multiplexador_2_1 (
  input  control,
  input  A,
  input  B,
  output out_4
);

  wire and_1_out, and_2_out, not_1_out;

  not not_1 (not_1_out, control);
  and and_1 (and_1_out, not_1_out, A);
  or or_1 (out_4, and_1_out, and_2_out);
  and and_2 (and_2_out, B, control);
endmodule

module Multiplexador_4_1 (
  input  control0,
  input  control1,
  input  a,
  input  b,
  input  c,
  input  d,
  output out_7
);

  wire multiplexador_2_1_1_out_4, multiplexador_2_1_2_out_4;

  Multiplexador_2_1 multiplexador_2_1_1 (.control(control0), .A(a), .B(b), .out_4(multiplexador_2_1_1_out_4));
  Multiplexador_2_1 multiplexador_2_1_2 (.control(control0), .A(c), .B(d), .out_4(multiplexador_2_1_2_out_4));
  Multiplexador_2_1 multiplexador_2_1_3 (
    .control(control1), .A(multiplexador_2_1_1_out_4), .B(multiplexador_2_1_2_out_4), .out_4(out_7));
endmodule

module Multiplexador_8_1 (
  input  control0,
  input  control1,
  input  control2,
  input  a,
  input  b,
  input  c,
  input  d,
  input  e,
  input  f,
  input  g,
  input  h,
  output out_12
);

  wire multiplexador_4_1_1_out_7, multiplexador_4_1_2_out_7;

  Multiplexador_4_1 multiplexador_4_1_1 (
    .control0(control0), .control1(control1), .a(a), .b(b), .c(c), .d(d), .out_7(multiplexador_4_1_1_out_7));
  Multiplexador_2_1 multiplexador_2_1_1 (
    .control(control2), .A(multiplexador_4_1_1_out_7), .B(multiplexador_4_1_2_out_7), .out_4(out_12));
  Multiplexador_4_1 multiplexador_4_1_2 (
    .control0(control0), .control1(control1), .a(e), .b(f), .c(g), .d(h), .out_7(multiplexador_4_1_2_out_7));
endmodule

module adder (
  input  A,
  input  B,
  input  CarryIn,
  output carryOut,
  output Sum
);

  wire and_1_out, and_2_out, xor_1_out;

  or or_1 (carryOut, and_1_out, and_2_out);
  and and_1 (and_1_out, A, B);
  and and_2 (and_2_out, CarryIn, xor_1_out);
  xor xor_1 (xor_1_out, A, B);
  xor xor_2 (Sum, CarryIn, xor_1_out);

  // Notes on the sheet:
  //   carry das entradas
  //   carry do carry in
endmodule

module add_sub_4bit (
  input  a3,
  input  b3,
  input  a2,
  input  b2,
  input  a1,
  input  b1,
  input  a0,
  input  b0,
  input  Sub,
  output CarryOut,
  output s3,
  output s2,
  output s1,
  output s0
);

  wire adder_2_carryout, adder_3_carryout, adder_4_carryout, xor_1_out, xor_2_out, xor_3_out, xor_4_out;

  xor xor_1 (xor_1_out, b3, Sub);
  adder adder_1 (.carryOut(CarryOut), .A(a3), .B(xor_1_out), .Sum(s3), .CarryIn(adder_2_carryout));
  adder adder_2 (.carryOut(adder_2_carryout), .A(a2), .B(xor_2_out), .Sum(s2), .CarryIn(adder_3_carryout));
  xor xor_2 (xor_2_out, b2, Sub);
  xor xor_3 (xor_3_out, b1, Sub);
  adder adder_3 (.carryOut(adder_3_carryout), .A(a1), .B(xor_3_out), .Sum(s1), .CarryIn(adder_4_carryout));
  xor xor_4 (xor_4_out, b0, Sub);
  adder adder_4 (.carryOut(adder_4_carryout), .A(a0), .B(xor_4_out), .Sum(s0), .CarryIn(Sub));
endmodule

module Demultiplexador_1_2 (
  input  control,
  input  \input ,
  output out_3,
  output out_4
);

  wire not_1_out;

  not not_1 (not_1_out, control);
  and and_1 (out_3, not_1_out, \input );
  and and_2 (out_4, control, \input );
endmodule

module Demultiplexador_1_8 (
  input  control0,
  input  control1,
  input  control2,
  input  \input ,
  output _0,
  output _1,
  output _2,
  output _3,
  output _4,
  output _5,
  output _6,
  output _7
);

  wire demultiplexador_1_2_1_out_3, demultiplexador_1_2_1_out_4, demultiplexador_1_2_2_out_3,
       demultiplexador_1_2_2_out_4, demultiplexador_1_2_3_out_3, demultiplexador_1_2_3_out_4;

  Demultiplexador_1_2 demultiplexador_1_2_1 (
    .control(control2), .\input (\input ), .out_3(demultiplexador_1_2_1_out_3),
    .out_4(demultiplexador_1_2_1_out_4));
  Demultiplexador_1_2 demultiplexador_1_2_2 (
    .control(control1), .\input (demultiplexador_1_2_1_out_3), .out_3(demultiplexador_1_2_2_out_3),
    .out_4(demultiplexador_1_2_2_out_4));
  Demultiplexador_1_2 demultiplexador_1_2_3 (
    .control(control1), .\input (demultiplexador_1_2_1_out_4), .out_3(demultiplexador_1_2_3_out_3),
    .out_4(demultiplexador_1_2_3_out_4));
  Demultiplexador_1_2 demultiplexador_1_2_4 (
    .control(control0), .\input (demultiplexador_1_2_2_out_3), .out_3(_0), .out_4(_1));
  Demultiplexador_1_2 demultiplexador_1_2_5 (
    .control(control0), .\input (demultiplexador_1_2_2_out_4), .out_3(_2), .out_4(_3));
  Demultiplexador_1_2 demultiplexador_1_2_6 (
    .control(control0), .\input (demultiplexador_1_2_3_out_3), .out_3(_4), .out_4(_5));
  Demultiplexador_1_2 demultiplexador_1_2_7 (
    .control(control0), .\input (demultiplexador_1_2_3_out_4), .out_3(_6), .out_4(_7));
endmodule

module Unidade_de_controle (
  input  op2,
  input  op1,
  input  op0,
  output ALUOp_1,
  output ALUOp_0,
  output ALUSrc,
  output RegWrite
);

  nand nand_1 (RegWrite, op1, op2);
  and and_1 (ALUSrc, RegWrite, op0);

  assign ALUOp_0 = op1;
  assign ALUOp_1 = op2;

  // Notes on the sheet:
  //   011 = subI
  //   101 = movI
  //   000 = sumR
  //   001 = sumI
  //   010 = subR
  //   100 = movR
  //   11x = exULA (forcar saida ula de valor do registrador - mov sem RegWrite)
endmodule

module Multiplexador_8_4 (
  input  control,
  input  x3,
  input  x2,
  input  x1,
  input  x0,
  input  y3,
  input  y2,
  input  y1,
  input  y0,
  output _3,
  output _2,
  output _1,
  output _0
);

  Multiplexador_2_1 multiplexador_2_1_1 (.control(control), .A(x3), .B(y3), .out_4(_3));
  Multiplexador_2_1 multiplexador_2_1_2 (.control(control), .A(x2), .B(y2), .out_4(_2));
  Multiplexador_2_1 multiplexador_2_1_3 (.control(control), .A(x1), .B(y1), .out_4(_1));
  Multiplexador_2_1 multiplexador_2_1_4 (.control(control), .A(x0), .B(y0), .out_4(_0));
endmodule

module Expansor_3_4bits (
  input  _2,
  input  _1,
  input  _0,
  output _3,
  output _2_2,
  output _1_2,
  output _0_2
);


  assign _0_2 = _0;
  assign _1_2 = _1;
  assign _2_2 = _2;
  assign _3 = 1'b0;
endmodule

module Decod_display_7_segmentos (
  input  _3,
  input  _2,
  input  _1,
  input  _0,
  output a,
  output b,
  output c,
  output d,
  output e,
  output f,
  output g
);

  wire and_1_out, and_2_out, and_3_out, and_4_out, and_5_out, and_6_out, and_7_out, and_8_out, and_9_out,
       and_10_out, and_11_out, and_12_out, and_13_out, and_14_out, and_15_out, and_16_out, not_1_out,
       not_2_out, not_3_out, not_4_out, not_5_out, not_6_out, not_7_out, not_8_out, not_9_out, not_10_out,
       not_11_out, not_12_out, not_13_out, not_14_out, not_15_out, not_16_out, not_17_out, not_18_out,
       not_19_out, not_20_out, not_21_out, or_1_out, or_2_out, or_3_out, or_4_out, or_5_out, or_6_out,
       or_8_out, or_11_out, or_12_out, or_14_out, or_15_out;

  not not_1 (not_1_out, _0);
  not not_2 (not_2_out, _2);
  not not_3 (not_3_out, _2);
  not not_4 (not_4_out, _0);
  not not_5 (not_5_out, _1);
  not not_6 (not_6_out, _0);
  not not_7 (not_7_out, _2);
  not not_8 (not_8_out, _0);
  not not_9 (not_9_out, _1);
  not not_10 (not_10_out, _0);
  not not_11 (not_11_out, _1);
  not not_12 (not_12_out, _0);
  not not_13 (not_13_out, _2);
  not not_14 (not_14_out, _0);
  not not_15 (not_15_out, _1);
  or or_1 (or_1_out, _3, _1);
  and and_1 (and_1_out, _2, _0);
  not not_16 (not_16_out, _2);
  and and_2 (and_2_out, not_16_out, not_17_out);
  not not_17 (not_17_out, _0);
  not not_18 (not_18_out, _2);
  not not_19 (not_19_out, _1);
  and and_3 (and_3_out, not_19_out, not_20_out);
  not not_20 (not_20_out, _0);
  and and_4 (and_4_out, _1, _0);
  not not_21 (not_21_out, _1);
  or or_2 (or_2_out, not_21_out, _0);
  or or_3 (or_3_out, _3, and_5_out);
  and and_5 (and_5_out, _1, not_1_out);
  and and_6 (and_6_out, not_2_out, _1);
  and and_7 (and_7_out, not_3_out, not_4_out);
  and and_8 (and_8_out, _2, not_5_out);
  and and_9 (and_9_out, and_8_out, _0);
  and and_10 (and_10_out, _1, not_6_out);
  and and_11 (and_11_out, not_7_out, not_8_out);
  or or_4 (or_4_out, _3, and_12_out);
  and and_12 (and_12_out, not_9_out, not_10_out);
  and and_13 (and_13_out, _2, not_11_out);
  and and_14 (and_14_out, _2, not_12_out);
  and and_15 (and_15_out, not_13_out, _1);
  or or_5 (or_5_out, not_14_out, not_15_out);
  or or_6 (or_6_out, or_1_out, and_1_out);
  or or_7 (a, or_6_out, and_2_out);
  or or_8 (or_8_out, not_18_out, and_3_out);
  or or_9 (b, or_8_out, and_4_out);
  or or_10 (c, or_2_out, _2);
  or or_11 (or_11_out, or_3_out, and_6_out);
  or or_12 (or_12_out, or_11_out, and_7_out);
  or or_13 (e, and_10_out, and_11_out);
  or or_14 (or_14_out, or_4_out, and_13_out);
  or or_15 (or_15_out, _3, and_15_out);
  or or_16 (g, or_15_out, and_16_out);
  and and_16 (and_16_out, _2, or_5_out);
  or or_17 (d, or_12_out, and_9_out);
  or or_18 (f, or_14_out, and_14_out);

  // Notes on the sheet:
  //   a = A + C + BD + B'C'
  //   b = B' + C'D' + CD
  //   c = C' + D + B
  //   d = A + CD' + B'C + B'D' + BC'D
  //   e = CD' + B'D'
  //   f = A + C'D' + BC' + BD'
  //   g = A + B'C + BD' + B C'
  //   g = A + B'C + B(D' +C')
endmodule

module Decod_novo_display_7seg (
  input  A,
  input  B,
  input  C,
  input  D,
  output a_2,
  output b_2,
  output c_2,
  output d_2,
  output e,
  output f,
  output g
);

  wire A_B_prime_out, A_C_out, B_prime_D_prime_out, BD_out, C_prime_D_prime_out, CD_out, not_1_out,
       not_2_out, not_3_out, not_4_out, or_1_out, or_2_out;

  not not_1 (not_1_out, A);
  not not_2 (not_2_out, B);
  not not_3 (not_3_out, C);
  not not_4 (not_4_out, D);
  or A_C (A_C_out, A, C);
  and BD (BD_out, B, D);
  and C_prime_D_prime (C_prime_D_prime_out, not_4_out, not_3_out);
  or or_1 (or_1_out, A_C_out, BD_out);
  and B_prime_D_prime (B_prime_D_prime_out, not_2_out, not_4_out);
  or A_B_prime (A_B_prime_out, not_2_out, A);
  or or_2 (or_2_out, C_prime_D_prime_out, CD_out);
  and CD (CD_out, D, C);
  or or_3 (a_2, or_1_out, B_prime_D_prime_out);
  or or_4 (b_2, A_B_prime_out, or_2_out);

  // Notes on the sheet:
  //   a = C + A + BD + B’D’
  //   b = C’D’ + CD + A + B’
  //   c = C’ + D + B + A
  //   d = B’(C + D’) + A + CD’ +  BC’D
  //   e = D’(B’ + C)
  //   f = C’D’ + A + B(D’ + C’)
  //   g = A + BC’ +CD’ + B’C
endmodule
